# Fritzing sketch Button_circuit (saved by Fritzing 0.8.7b)

parts:
  Nano1 = Arduino Nano v2.3
  S1 = Round Pushbutton
  U1 = RF-LINK_TX [package=rf-link_tx]

nets:
  N1: Nano1.D2, U1.DATA
  N2: Nano1.D4, S1.leg0
  +5V: Nano1.+5V, U1.+5V
  GND: Nano1.GND, U1.GND
